# Fritzing sketch plans V1 (saved by Fritzing 0.9.2b)
breadboards: 1

parts:
  Composant1 = Arduino Uno (Rev3)
  S1 = Pushbutton [package="[THT]"]
  S2 = Pushbutton [package="[THT]"]
  S3 = Pushbutton [package="[THT]"]
  R1 = Resistor [tolerance=±5% resistance=10k package=THT]
  R2 = Resistor [tolerance=±5% resistance=10k package=THT]
  R3 = Resistor [tolerance=±5% resistance=10k package=THT]
  LCD1 = LCD screen
  R4 = Resistor [tolerance=±5% resistance=220 package=THT]
  LED1 = LED - 5mm [color="Red (633nm)" package="5 mm [THT]"]
  R5 = Resistor [tolerance=±5% resistance=220 package=THT]

nets:
  N1: Composant1.D8, S3.Pin_1, S3.Pin_2, R1.Pin_0
  N2: Composant1.D9_PWM, S2.Pin_1, S2.Pin_2, R2.Pin_0
  N3: Composant1.D10_PWM/SS, S1.Pin_1, S1.Pin_2, R3.Pin_0
  N4: Composant1.D11_PWM/MOSI, LED1.anode
  N5: Composant1.D2, LCD1.RS
  N6: Composant1.D3_PWM, LCD1.E, LCD1.DB0
  N7: Composant1.D4, LCD1.DB4
  N8: Composant1.D5_PWM, LCD1.DB5
  N9: Composant1.D6_PWM, LCD1.DB6
  N10: Composant1.D7, LCD1.DB7
  5V: Composant1.5V, S1.Pin_3, S1.Pin_4, S2.Pin_3, S2.Pin_4, S3.Pin_3, S3.Pin_4, LCD1.VDD, R4.Pin_0
  GND: Composant1.GND, R1.Pin_1, R2.Pin_1, R3.Pin_1, LCD1.VSS, LCD1.V0, LCD1.R/W, LCD1.LED-, R5.Pin_0
  N11: LCD1.LED+, R4.Pin_1
  N12: LED1.cathode, R5.Pin_1

notes:
  réglages / h / min
